# Fritzing sketch collison-deector (saved by Fritzing 0.9.3b)
breadboards: 1

parts:
  Raspberry_Pi_1 = Raspberry Pi 3 [part_number=RPI-3-V1.2]
  hc-sr1 = hc-sr04
  LED1 = smd LED [color="Green (555nm)" package="0603 [SMD]"]
  LED2 = smd LED [color="Red (633nm)" package="0603 [SMD]"]
  LED3 = smd LED [color="Yellow (592nm)" package="0603 [SMD]"]
  R1 = Resistor [tolerance=±5% resistance=1k package=THT]
  R2 = Resistor [tolerance=±5% resistance=1k package=THT]
  R3 = Resistor [tolerance=±5% resistance=1k package=THT]

nets:
  N1: Raspberry_Pi_1.GPIO17, LED3.anode
  N2: Raspberry_Pi_1.GPIO27, LED2.anode
  N3: Raspberry_Pi_1.GPIO22, LED1.anode
  N4: Raspberry_Pi_1.GPIO5, hc-sr1.Trig
  N5: Raspberry_Pi_1.GPIO6, hc-sr1.Echo
  GND: Raspberry_Pi_1.GND, hc-sr1.GND, R1.Pin_1, R2.Pin_1, R3.Pin_1
  5V: Raspberry_Pi_1.5V, hc-sr1.VCC
  N6: LED1.cathode, R1.Pin_0
  N7: LED2.cathode, R2.Pin_0
  N8: LED3.cathode, R3.Pin_0
